# Fritzing sketch mando_0.1 (saved by Fritzing 0.9.3b)
breadboards: 1

parts:
  Componente1 = Arduino Uno (Rev3)
  S1 = Pushbutton [package="[THT]"]
  S2 = Pushbutton [package="[THT]"]
  S3 = Pushbutton [package="[THT]"]
  S4 = Pushbutton [package="[THT]"]
  R1 = Resistor [tolerance=±5% resistance=220 package=THT]
  R2 = Resistor [tolerance=±5% resistance=220 package=THT]
  R3 = Resistor [tolerance=±5% resistance=220 package=THT]
  R4 = Resistor [tolerance=±5% resistance=220 package=THT]
  LED1 = LED - 5mm [color="Red (633nm)" package="5 mm [THT]"]
  LED2 = LED - 5mm [color="Red (633nm)" package="5 mm [THT]"]
  R5 = Resistor [tolerance=±5% resistance=220 package=THT]
  R6 = Resistor [tolerance=±5% resistance=220 package=THT]

nets:
  N1: Componente1.D2, S4.Pin_1, R4.Pin_1
  N2: Componente1.D3_PWM, S3.Pin_1, S3.Pin_2, R2.Pin_1
  N3: Componente1.D4, S2.Pin_1, R3.Pin_1
  N4: Componente1.D5_PWM, S1.Pin_1, R1.Pin_0
  N5: Componente1.D6_PWM, R6.Pin_0
  N6: Componente1.D7, R5.Pin_0
  N7: Componente1.GND, R1.Pin_1, R2.Pin_0, R3.Pin_0, R4.Pin_0, LED1.cathode, LED2.cathode
  N8: LED1.anode, R5.Pin_1
  N9: LED2.anode, R6.Pin_1
